// Logisim project dekoder.circ as structural Verilog: 1 circuit, main circuit main
module main (
  input  [2:0] in_1,
  input  [2:0] in_2,
  input  [2:0] in_3
);

  wire nand_1_out, nand_2_out, not_1_out, not_2_out, or_1_out, or_2_out, xor_1_out, xor_2_out;

  xor xor_1 (xor_1_out, in_1[0], in_1[2]);
  not not_1 (not_1_out, in_1[1]);
  or or_1 (or_1_out, in_3[0], in_3[2]);
  xor xor_2 (xor_2_out, in_2[0], in_2[1]);
  _7_Segment_Display u_7_segment_display_1 (.c(or_2_out));  // open: g, f, a, b, e, d, dp
  not not_2 (not_2_out, in_3[1]);
  or or_2 (or_2_out, not_2_out, or_1_out);
  _7_Segment_Display u_7_segment_display_2 (.a(nand_1_out));  // open: g, f, b, e, d, c, dp
  nand nand_1 (nand_1_out, xor_1_out, not_1_out);
  _7_Segment_Display u_7_segment_display_3 (.b(nand_2_out));  // open: g, f, a, e, d, c, dp
  nand nand_2 (nand_2_out, xor_2_out, in_2[2]);

  // Notes on the sheet:
  //   A
  //   B
  //   C
endmodule
